// Logisim project tennis.circ as structural Verilog: 18 circuits, main circuit main
module main (
);

  wire and_2_out, cdm_8_mark5_1_p6, cdm_8_mark5_1_p7, clk, clk1, comparator_1_eq, d_ff_1_q, d_ff_2_q,
       decoder_1_out0, decoder_1_out1, IAck, IOsel, IRQ, multiplexer_2_out, multiplexer_4_out, not_1_out,
       not_2_out, of, or_1_out, READwrite, Reset_out;
  wire [1:0] joystick_1_y;
  wire [2:0] cnt, vec;
  wire [4:0] kinematic_controller_1_ballx, kinematic_controller_1_bally, kinematic_controller_1_leftyout,
       kinematic_controller_1_out_5, kinematic_controller_1_rightyout, video_section_1_out_14,
       video_section_1_out_15, video_section_1_out_16, video_section_1_out_17, video_section_1_out_18,
       video_section_2_out_14, video_section_2_out_15, video_section_2_out_16, video_section_2_out_17,
       video_section_2_out_18, video_section_3_out_14, video_section_3_out_15, video_section_3_out_16,
       video_section_3_out_17, video_section_3_out_18;
  wire [7:0] adress, batxadr, batxdat, batydat, bit_extender_1_out, cdm8_bat, cdm8_score, cdm_8_mark5_1_p10,
       cdm_8_mark5_1_p11, IOdat, multiplexer_1_out, multiplexer_3_out, pc, player_score, plycoorddat,
       scoredata, vxdat, vydat;
  wire [31:0] video_section_1_out_6, video_section_1_out_7, video_section_1_out_8, video_section_1_out_9,
       video_section_1_out_10, video_section_1_out_11, video_section_1_out_12, video_section_1_out_13,
       video_section_2_out_6, video_section_2_out_7, video_section_2_out_8, video_section_2_out_9,
       video_section_2_out_10, video_section_2_out_11, video_section_2_out_12, video_section_2_out_13,
       video_section_3_out_6, video_section_3_out_7, video_section_3_out_8, video_section_3_out_9,
       video_section_3_out_10, video_section_3_out_11, video_section_3_out_12, video_section_3_out_13,
       video_section_4_out_6, video_section_4_out_7, video_section_4_out_8, video_section_4_out_9,
       video_section_4_out_10, video_section_4_out_11, video_section_4_out_12, video_section_4_out_13;

  Joystick #(.bits(2)) joystick_1 (.y(joystick_1_y));  // open: x
  LED led_1 ();  // open: in
  LED led_2 ();  // open: in
  LED led_3 ();  // open: in
  LED led_4 ();  // open: in
  Hex_Digit_Display hex_digit_display_1 ();  // open: value, dp
  // score_main main_1: pin names not known; wires that end beside it: player_score
  Multiplexer #(.select(3), .width(8)) multiplexer_1 (
    .in0(batxadr), .in1(batxadr), .in2(batxadr), .in3(batxadr), .in4(batxadr), .in5(batxadr), .in6(batxadr),
    .in7(adress), .out(multiplexer_1_out), .sel(cnt));  // open: en
  // Probe on pc
  Multiplexer multiplexer_2 (.in0(1'b0), .in1(clk), .out(multiplexer_2_out), .sel(d_ff_2_q));  // open: en
  LED led_5 ();  // open: in
  LED led_6 ();  // open: in
  LED led_7 ();  // open: in
  LED led_8 ();  // open: in
  Hex_Digit_Display hex_digit_display_2 ();  // open: value, dp
  Button Reset (.out(Reset_out));
  DotMatrix #(.matrixcols(32), .matrixrows(32)) dotmatrix_1 (
    .col0(video_section_1_out_6), .col1(video_section_1_out_7), .col2(video_section_1_out_8),
    .col3(video_section_1_out_9), .col4(video_section_1_out_10), .col5(video_section_1_out_11),
    .col6(video_section_1_out_12), .col7(video_section_1_out_13), .col8(video_section_2_out_6),
    .col9(video_section_2_out_7), .col10(video_section_2_out_8), .col11(video_section_2_out_9),
    .col12(video_section_2_out_10), .col13(video_section_2_out_11), .col14(video_section_2_out_12),
    .col15(video_section_2_out_13), .col16(video_section_3_out_6), .col17(video_section_3_out_7),
    .col18(video_section_3_out_8), .col19(video_section_3_out_9), .col20(video_section_3_out_10),
    .col21(video_section_3_out_11), .col22(video_section_3_out_12), .col23(video_section_3_out_13),
    .col24(video_section_4_out_6), .col25(video_section_4_out_7), .col26(video_section_4_out_8),
    .col27(video_section_4_out_9), .col28(video_section_4_out_10), .col29(video_section_4_out_11),
    .col30(video_section_4_out_12), .col31(video_section_4_out_13));
  kinematic_controller kinematic_controller_1 (
    .button_up(joystick_1_y), .vx(vxdat), .scoreA(player_score), .scoreB(cdm8_score),
    .out_5(kinematic_controller_1_out_5), .ballX(kinematic_controller_1_ballx),
    .ballY(kinematic_controller_1_bally), .leftYout(kinematic_controller_1_leftyout),
    .rightYout(kinematic_controller_1_rightyout), .reset(Reset_out), .in_4(cdm8_bat), .vy(vydat),
    .ball_x(batxdat), .ball_y(batydat), .rightBat(cdm8_bat));  // open: leftYin
  // CdM_8_mark5 cdm_8_mark5_1: pin names not known; wires that end beside it: IRQ, vec, IAck, multiplexer_2_out, pc, cdm_8_mark5_1_p6, cdm_8_mark5_1_p7, READwrite, adress, cdm_8_mark5_1_p10, cdm_8_mark5_1_p11
  LED led_9 ();  // open: in
  LED led_10 ();  // open: in
  LED led_11 ();  // open: in
  LED led_12 ();  // open: in
  video_section video_section_1 (
    .in_1(kinematic_controller_1_out_5), .in_2(kinematic_controller_1_ballx),
    .in_3(kinematic_controller_1_bally), .in_4(kinematic_controller_1_leftyout),
    .in_5(kinematic_controller_1_rightyout), .out_14(video_section_1_out_14),
    .out_15(video_section_1_out_15), .out_16(video_section_1_out_16), .out_17(video_section_1_out_17),
    .out_18(video_section_1_out_18), .out_6(video_section_1_out_6), .out_7(video_section_1_out_7),
    .out_8(video_section_1_out_8), .out_9(video_section_1_out_9), .out_10(video_section_1_out_10),
    .out_11(video_section_1_out_11), .out_12(video_section_1_out_12), .out_13(video_section_1_out_13));
  Multiplexer #(.select(3), .width(8)) multiplexer_3 (
    .in0(scoredata), .in1(plycoorddat), .in2(cdm8_bat), .in3(batxdat), .in4(batydat), .in5(vxdat),
    .in6(vydat), .in7(IOdat), .out(multiplexer_3_out), .sel(cnt));  // open: en
  LED led_13 ();  // open: in
  LED led_14 ();  // open: in
  LED led_15 ();  // open: in
  LED led_16 ();  // open: in
  video_section video_section_2 (
    .in_1(video_section_1_out_14), .in_2(video_section_1_out_15), .in_3(video_section_1_out_16),
    .in_4(video_section_1_out_17), .in_5(video_section_1_out_18), .out_14(video_section_2_out_14),
    .out_15(video_section_2_out_15), .out_16(video_section_2_out_16), .out_17(video_section_2_out_17),
    .out_18(video_section_2_out_18), .out_6(video_section_2_out_6), .out_7(video_section_2_out_7),
    .out_8(video_section_2_out_8), .out_9(video_section_2_out_9), .out_10(video_section_2_out_10),
    .out_11(video_section_2_out_11), .out_12(video_section_2_out_12), .out_13(video_section_2_out_13));
  // Probe on multiplexer_3_out
  and and_1 (IOsel, adress[4], adress[5], adress[6], adress[7], decoder_1_out1);
  Decoder #(.disabled(0)) decoder_1 (
    .out0(decoder_1_out0), .out1(decoder_1_out1), .sel(cdm_8_mark5_1_p6), .en(cdm_8_mark5_1_p7));
  not not_1 (not_1_out, READwrite);
  assign IOdat = not_1_out ? cdm_8_mark5_1_p10 : 8'bz;  // Controlled_Buffer controlled_buffer_1
  assign cdm_8_mark5_1_p11 = READwrite ? IOdat : 8'bz;  // Controlled_Buffer controlled_buffer_2
  LED led_17 ();  // open: in
  LED led_18 ();  // open: in
  LED led_19 ();  // open: in
  LED led_20 ();  // open: in
  video_section video_section_3 (
    .in_1(video_section_2_out_14), .in_2(video_section_2_out_15), .in_3(video_section_2_out_16),
    .in_4(video_section_2_out_17), .in_5(video_section_2_out_18), .out_14(video_section_3_out_14),
    .out_15(video_section_3_out_15), .out_16(video_section_3_out_16), .out_17(video_section_3_out_17),
    .out_18(video_section_3_out_18), .out_6(video_section_3_out_6), .out_7(video_section_3_out_7),
    .out_8(video_section_3_out_8), .out_9(video_section_3_out_9), .out_10(video_section_3_out_10),
    .out_11(video_section_3_out_11), .out_12(video_section_3_out_12), .out_13(video_section_3_out_13));
  // Probe on adress
  and and_2 (and_2_out, decoder_1_out1, ~IOsel);  // AND_Gate
  LED led_21 ();  // open: in
  LED led_22 ();  // open: in
  LED led_23 ();  // open: in
  LED led_24 ();  // open: in
  // score_main main_2: pin names not known; wires that end beside it: cdm8_score
  Hex_Digit_Display hex_digit_display_3 ();  // open: value, dp
  video_section video_section_4 (
    .in_1(video_section_3_out_14), .in_2(video_section_3_out_15), .in_3(video_section_3_out_16),
    .in_4(video_section_3_out_17), .in_5(video_section_3_out_18), .out_6(video_section_4_out_6),
    .out_7(video_section_4_out_7), .out_8(video_section_4_out_8), .out_9(video_section_4_out_9),
    .out_10(video_section_4_out_10), .out_11(video_section_4_out_11), .out_12(video_section_4_out_12),
    .out_13(video_section_4_out_13));  // open: out_14, out_15, out_16, out_17, out_18
  // Probe on multiplexer_1_out
  or or_1 (or_1_out, and_2_out, ~of);  // OR_Gate
  LED led_25 ();  // open: in
  LED led_26 ();  // open: in
  LED led_27 ();  // open: in
  LED led_28 ();  // open: in
  Hex_Digit_Display hex_digit_display_4 ();  // open: value, dp
  RAM #(.bus("separate")) ram_1 (
    .addr(multiplexer_1_out), .din(multiplexer_3_out), .data(IOdat), .sel(or_1_out), .clk(not_2_out),
    .ld(multiplexer_4_out));  // open: str, clr
  Multiplexer multiplexer_4 (.in0(1'b0), .in1(READwrite), .out(multiplexer_4_out), .sel(of));  // open: en
  not not_2 (not_2_out, clk);
  ROM rom_1 (.addr(adress), .data(IOdat), .sel(decoder_1_out0));
  LED led_29 ();  // open: in
  LED led_30 ();  // open: in
  LED led_31 ();  // open: in
  LED led_32 ();  // open: in
  // Probe on IOdat
  Clock clock_1 (.out(clk));
  Multiplexer multiplexer_5 (.in0(clk), .in1(1'b0), .out(clk1), .sel(d_ff_1_q));  // open: en
  D_Flip_Flop d_ff_1 (.clk(of), .D(of), .Q(d_ff_1_q), .reset(comparator_1_eq));  // open: Qn, preset, en
  D_Flip_Flop #(.trigger("high")) d_ff_2 (.clk(d_ff_1_q), .D(d_ff_1_q), .Q(d_ff_2_q));  // open: Qn, preset, en, reset
  assign bit_extender_1_out = {{5{1'b0}}, cnt};  // Bit_Extender bit_extender_1
  Counter #(.width(3), .max('h7)) counter_1 (
    .count(clk1), .Q(cnt), .carry(of), .clk(clk1), .clr(comparator_1_eq));  // open: load, D
  Comparator comparator_1 (.a(pc), .b(8'h32), .eq(comparator_1_eq));  // open: gt, lt
  Adder adder_1 (.a(8'he1), .b(bit_extender_1_out), .out(batxadr));  // open: cin, cout

  // Other names for the same wires on the sheet: IOaddr[3:0] = adress[3:0]; batyadr[7:0] = batxadr;
  //   cdmyadr[7:0] = batxadr; plycoordadr[7:0] = batxadr; scoreadr[7:0] = batxadr; vxadr[7:0] = batxadr;
  //   vyadr[7:0] = batxadr

  // Notes on the sheet:
  //   contents of rom_1 (hex, n*v repeats v):
  //   cd f0 d0 e4 b0 d2 e0 38 d2 e5 ba 18 98 d2 e7 ba 3 a e0 18 1c 8a ee 11 d3 ff 33 d0 e3 b4 c 7d ea 26
  //   d2 ff ee 28 d2 1 7d e0 2e 19 ee 28 d2 e3 ab ee 2 d4
endmodule

module video_chip (
  input  [4:0] chipID,
  input  [4:0] ballX,
  input  [4:0] ballY,
  input  [4:0] leftBat,
  input  [4:0] rightBat,
  output [4:0] nextChipID,
  output [4:0] ballX_2,
  output [4:0] ballY_2,
  output [4:0] leftBat_2,
  output [4:0] rightBat_2
);

  inc_5_bit inc_5_bit_1 (.in_1(chipID), .out_2(nextChipID));

  assign ballX_2 = ballX;
  assign ballY_2 = ballY;
  assign leftBat_2 = leftBat;
  assign rightBat_2 = rightBat;
endmodule

// inc
module inc_5_bit (
  input  [4:0] in_1,
  output [4:0] out_2
);

  wire [4:0] and_1_out;

  assign and_1_out = {and_1_out[3:0], 1'b1} & in_1;  // AND_Gate and_1, 5 bits wide
  assign out_2 = in_1 ^ {and_1_out[3:0], 1'b1};  // XOR_Gate xor_1, 5 bits wide
  // also tied to GND on the sheet: and_1_out[4]
endmodule

module video_section (
  input  [4:0] in_1,
  input  [4:0] in_2,
  input  [4:0] in_3,
  input  [4:0] in_4,
  input  [4:0] in_5,
  output [31:0] out_6,
  output [31:0] out_7,
  output [31:0] out_8,
  output [31:0] out_9,
  output [31:0] out_10,
  output [31:0] out_11,
  output [31:0] out_12,
  output [31:0] out_13,
  output [4:0] out_14,
  output [4:0] out_15,
  output [4:0] out_16,
  output [4:0] out_17,
  output [4:0] out_18
);

  wire comparator_1_eq, comparator_2_eq, comparator_3_eq, comparator_4_eq, comparator_5_eq, comparator_6_eq,
       comparator_7_eq, comparator_8_eq, comparator_9_eq, comparator_10_eq, not_1_out, not_2_out;
  wire [4:0] ID1, ID2, ID3, ID4, ID5, ID6, ID7, video_chip_1_ballx_2, video_chip_1_bally_2,
       video_chip_1_leftbat_2, video_chip_1_rightbat_2, video_chip_2_ballx_2, video_chip_2_bally_2,
       video_chip_2_leftbat_2, video_chip_2_rightbat_2, video_chip_3_ballx_2, video_chip_3_bally_2,
       video_chip_3_leftbat_2, video_chip_3_rightbat_2, video_chip_4_ballx_2, video_chip_4_bally_2,
       video_chip_4_leftbat_2, video_chip_4_rightbat_2, video_chip_5_ballx_2, video_chip_5_bally_2,
       video_chip_5_leftbat_2, video_chip_5_rightbat_2, video_chip_6_ballx_2, video_chip_6_bally_2,
       video_chip_6_leftbat_2, video_chip_6_rightbat_2, video_chip_7_ballx_2, video_chip_7_bally_2,
       video_chip_7_leftbat_2, video_chip_7_rightbat_2;
  wire [31:0] bat_l_32, bat_r_32, multiplexer_2_out, multiplexer_3_out, multiplexer_8_out, multiplexer_9_out,
       y;

  Multiplexer #(.width(32)) multiplexer_1 (.in0({32{1'b0}}), .in1(y), .out(out_6), .sel(comparator_1_eq));  // open: en
  _5_to_32 u_5_to_32_1 (.in_1(in_3), .out_2(y));
  Multiplexer #(.width(32)) multiplexer_2 (
    .in0(bat_l_32), .in1({32{1'b0}}), .out(multiplexer_2_out), .sel(not_1_out));  // open: en
  Comparator #(.width(5)) comparator_1 (.a(in_1), .b(in_2), .eq(comparator_1_eq));  // open: gt, lt
  video_chip video_chip_1 (
    .chipID(in_1), .ballX(in_2), .ballY(in_3), .leftBat(in_4), .rightBat(in_5), .nextChipID(ID1),
    .ballX_2(video_chip_1_ballx_2), .ballY_2(video_chip_1_bally_2), .leftBat_2(video_chip_1_leftbat_2),
    .rightBat_2(video_chip_1_rightbat_2));
  assign out_7 = multiplexer_2_out | multiplexer_3_out;  // OR_Gate or_1, 32 bits wide
  not not_1 (not_1_out, comparator_3_eq);
  Multiplexer #(.width(32)) multiplexer_3 (
    .in0({32{1'b0}}), .in1(y), .out(multiplexer_3_out), .sel(comparator_2_eq));  // open: en
  Comparator #(.width(5)) comparator_2 (.a(ID1), .b(in_2), .eq(comparator_2_eq));  // open: gt, lt
  Comparator #(.width(5)) comparator_3 (.a(ID1), .b(5'b00001), .eq(comparator_3_eq));  // open: gt, lt
  bat bat_1 (.in_1(out_17), .out_2(bat_l_32));
  Multiplexer #(.width(32)) multiplexer_4 (.in0({32{1'b0}}), .in1(y), .out(out_8), .sel(comparator_4_eq));  // open: en
  Comparator #(.width(5)) comparator_4 (.a(ID2), .b(in_2), .eq(comparator_4_eq));  // open: gt, lt
  video_chip video_chip_2 (
    .chipID(ID1), .ballX(video_chip_1_ballx_2), .ballY(video_chip_1_bally_2),
    .leftBat(video_chip_1_leftbat_2), .rightBat(video_chip_1_rightbat_2), .nextChipID(ID2),
    .ballX_2(video_chip_2_ballx_2), .ballY_2(video_chip_2_bally_2), .leftBat_2(video_chip_2_leftbat_2),
    .rightBat_2(video_chip_2_rightbat_2));
  Multiplexer #(.width(32)) multiplexer_5 (.in0({32{1'b0}}), .in1(y), .out(out_9), .sel(comparator_5_eq));  // open: en
  Comparator #(.width(5)) comparator_5 (.a(ID3), .b(in_2), .eq(comparator_5_eq));  // open: gt, lt
  video_chip video_chip_3 (
    .chipID(ID2), .ballX(video_chip_2_ballx_2), .ballY(video_chip_2_bally_2),
    .leftBat(video_chip_2_leftbat_2), .rightBat(video_chip_2_rightbat_2), .nextChipID(ID3),
    .ballX_2(video_chip_3_ballx_2), .ballY_2(video_chip_3_bally_2), .leftBat_2(video_chip_3_leftbat_2),
    .rightBat_2(video_chip_3_rightbat_2));
  Multiplexer #(.width(32)) multiplexer_6 (.in0({32{1'b0}}), .in1(y), .out(out_10), .sel(comparator_6_eq));  // open: en
  video_chip video_chip_4 (
    .chipID(ID3), .ballX(video_chip_3_ballx_2), .ballY(video_chip_3_bally_2),
    .leftBat(video_chip_3_leftbat_2), .rightBat(video_chip_3_rightbat_2), .nextChipID(ID4),
    .ballX_2(video_chip_4_ballx_2), .ballY_2(video_chip_4_bally_2), .leftBat_2(video_chip_4_leftbat_2),
    .rightBat_2(video_chip_4_rightbat_2));
  Comparator #(.width(5)) comparator_6 (.a(ID4), .b(in_2), .eq(comparator_6_eq));  // open: gt, lt
  video_chip video_chip_5 (
    .chipID(ID4), .ballX(video_chip_4_ballx_2), .ballY(video_chip_4_bally_2),
    .leftBat(video_chip_4_leftbat_2), .rightBat(video_chip_4_rightbat_2), .nextChipID(ID5),
    .ballX_2(video_chip_5_ballx_2), .ballY_2(video_chip_5_bally_2), .leftBat_2(video_chip_5_leftbat_2),
    .rightBat_2(video_chip_5_rightbat_2));
  Multiplexer #(.width(32)) multiplexer_7 (.in0({32{1'b0}}), .in1(y), .out(out_11), .sel(comparator_7_eq));  // open: en
  Comparator #(.width(5)) comparator_7 (.a(ID5), .b(in_2), .eq(comparator_7_eq));  // open: gt, lt
  video_chip video_chip_6 (
    .chipID(ID5), .ballX(video_chip_5_ballx_2), .ballY(video_chip_5_bally_2),
    .leftBat(video_chip_5_leftbat_2), .rightBat(video_chip_5_rightbat_2), .nextChipID(ID6),
    .ballX_2(video_chip_6_ballx_2), .ballY_2(video_chip_6_bally_2), .leftBat_2(video_chip_6_leftbat_2),
    .rightBat_2(video_chip_6_rightbat_2));
  assign out_12 = multiplexer_8_out | multiplexer_9_out;  // OR_Gate or_2, 32 bits wide
  Multiplexer #(.width(32)) multiplexer_8 (
    .in0(bat_r_32), .in1({32{1'b0}}), .out(multiplexer_8_out), .sel(not_2_out));  // open: en
  Multiplexer #(.width(32)) multiplexer_9 (
    .in0({32{1'b0}}), .in1(y), .out(multiplexer_9_out), .sel(comparator_8_eq));  // open: en
  Comparator #(.width(5)) comparator_8 (.a(ID6), .b(in_2), .eq(comparator_8_eq));  // open: gt, lt
  Comparator #(.width(5), .mode("unsigned")) comparator_9 (
    .a(ID6), .b(5'b11110), .eq(comparator_9_eq));  // open: gt, lt
  bat bat_2 (.in_1(out_18), .out_2(bat_r_32));
  video_chip video_chip_7 (
    .chipID(ID6), .ballX(video_chip_6_ballx_2), .ballY(video_chip_6_bally_2),
    .leftBat(video_chip_6_leftbat_2), .rightBat(video_chip_6_rightbat_2), .nextChipID(ID7),
    .ballX_2(video_chip_7_ballx_2), .ballY_2(video_chip_7_bally_2), .leftBat_2(video_chip_7_leftbat_2),
    .rightBat_2(video_chip_7_rightbat_2));
  Multiplexer #(.width(32)) multiplexer_10 (
    .in0({32{1'b0}}), .in1(y), .out(out_13), .sel(comparator_10_eq));  // open: en
  not not_2 (not_2_out, comparator_9_eq);
  Comparator #(.width(5)) comparator_10 (.a(ID7), .b(in_2), .eq(comparator_10_eq));  // open: gt, lt
  video_chip video_chip_8 (
    .chipID(ID7), .ballX(video_chip_7_ballx_2), .ballY(video_chip_7_bally_2),
    .leftBat(video_chip_7_leftbat_2), .rightBat(video_chip_7_rightbat_2), .nextChipID(out_14),
    .ballX_2(out_15), .ballY_2(out_16), .leftBat_2(out_17), .rightBat_2(out_18));

  // Other names for the same wires on the sheet: bat_l[4:0] = out_17; bat_r[4:0] = out_18; ID0[4:0] = in_1;
  //   x[4:0] = in_2
endmodule

module inrange (
  input  [4:0] Yball,
  input  [4:0] Ybat,
  input  isTheSameX,
  output exit
);

  wire comparator_1_lt, comparator_2_gt, nor_1_out;
  wire [4:0] adder_1_out;

  // Probe on Yball
  // Probe on Ybat
  // Probe on adder_1_out
  Adder #(.width(5)) adder_1 (.a(5'b00011), .b(Ybat), .out(adder_1_out));  // open: cin, cout
  Comparator #(.width(5)) comparator_1 (.a(Yball), .b(Ybat), .lt(comparator_1_lt));  // open: gt, eq
  Comparator #(.width(5)) comparator_2 (.a(Yball), .b(adder_1_out), .gt(comparator_2_gt));  // open: eq, lt
  nor nor_1 (nor_1_out, comparator_1_lt, comparator_2_gt);
  assign exit = isTheSameX ? nor_1_out : 1'bz;  // Controlled_Buffer controlled_buffer_1
  Pull_Resistor pull_resistor_1 (.node(exit));
endmodule

module reflect (
  input  [2:0] in_1,
  output [2:0] out_2
);

  wire comparator_1_eq;
  wire [2:0] inc_3_bit_1_out_2, not_1_out, not_2_out;

  assign not_1_out = ~in_1;  // NOT_Gate not_1, 3 bits wide
  assign not_2_out = ~in_1;  // NOT_Gate not_2, 3 bits wide
  Comparator #(.width(3)) comparator_1 (.a(3'b100), .b(in_1), .eq(comparator_1_eq));  // open: gt, lt
  inc_3_bit inc_3_bit_1 (.in_1(not_2_out), .out_2(inc_3_bit_1_out_2));
  switch switch_1 (.in_1(not_1_out), .in_2(comparator_1_eq), .in_3(inc_3_bit_1_out_2), .out_4(out_2));
endmodule

module switch (
  input  [2:0] in_1,
  input  in_2,
  input  [2:0] in_3,
  output [2:0] out_4
);

  wire [2:0] and_1_out, and_2_out;
  wire [2:2] not_1_out;

  not not_1 (not_1_out[2], in_2);
  assign and_1_out = in_1 & {3{not_1_out[2]}};  // AND_Gate and_1, 3 bits wide
  assign and_2_out = {3{in_2}} & in_3;  // AND_Gate and_2, 3 bits wide
  assign out_4 = and_1_out | and_2_out;  // OR_Gate or_1, 3 bits wide
endmodule

module inc_3_bit (
  input  [2:0] in_1,
  output [2:0] out_2
);

  wire [2:0] and_1_out;

  assign and_1_out = {and_1_out[1:0], 1'b1} & in_1;  // AND_Gate and_1, 3 bits wide
  assign out_2 = in_1 ^ {and_1_out[1:0], 1'b1};  // XOR_Gate xor_1, 3 bits wide
  // also tied to GND on the sheet: and_1_out[2]
endmodule

// CONTROLLER
module kinematic_controller (
  input  [1:0] button_up,
  input  [4:0] leftYin,
  input  reset,
  input  [7:0] in_4,
  output [4:0] out_5,
  output [4:0] ballX,
  output [4:0] ballY,
  output [4:0] leftYout,
  output [4:0] rightYout,
  output [7:0] vx,
  output [7:0] vy,
  output [7:0] scoreA,
  output [7:0] scoreB,
  output [7:0] ball_x,
  output [7:0] ball_y,
  output [7:0] rightBat
);

  wire clock_1_out, clock_2_out, clock_3_out, clock_4_out, controlled_buffer_1_out, counter_3_q, down,
       hitTheLeftBall, hitTheRightBall, init, or_1_out, undriven, up, x, y;
  wire [2:0] left_bat_out, x_ball, y_ball;
  wire [7:0] left_bat_temp, multiplexer_1_out, multiplexer_2_out, multiplexer_3_out, multiplexer_4_out, vx_t,
       vy_t;

  bat_move bat_move_1 (.in_1({leftYout, left_bat_out}), .in_2(up), .in_3(down), .bat_y(left_bat_temp));
  Comparator #(.width(2), .mode("unsigned")) comparator_1 (.a(2'b10), .b(button_up), .gt(up), .lt(down));  // open: eq
  check_hit check_hit_1 (
    .ball_x(ball_x), .x_hit(x), .left_bat(left_bat_temp), .vx(vx), .vy(vy), .ball_y(ball_y), .y_hit(y),
    .hitTheRightWall(hitTheRightBall), .hitTheLeftWall(hitTheLeftBall), .right_bat(in_4));
  Multiplexer #(.width(8)) multiplexer_1 (
    .in0({ballX, x_ball}), .in1(8'h64), .out(multiplexer_1_out), .sel(init));  // open: en
  assign controlled_buffer_1_out = or_1_out ? clock_1_out : 1'bz;  // Controlled_Buffer controlled_buffer_1
  Clock #(.highDuration(4), .lowDuration(4)) clock_1 (.out(clock_1_out));
  or or_1 (or_1_out, up, down);
  Register xreg (.D(multiplexer_1_out), .Q(ball_x), .clk(clock_2_out));  // open: en, clr
  Clock #(.highDuration(2), .lowDuration(2)) clock_2 (.out(clock_2_out));
  Multiplexer #(.width(8)) multiplexer_2 (.in0(vx_t), .in1(8'hfe), .out(multiplexer_2_out), .sel(init));  // open: en
  Register u_vx (.D(multiplexer_2_out), .Q(vx), .clk(clock_3_out));  // open: en, clr
  Clock #(.highDuration(2), .lowDuration(2)) clock_3 (.out(clock_3_out));
  Counter counter_1 (.count(hitTheRightBall), .Q(scoreA), .clk(clock_3_out), .clr(reset));  // open: load, D, carry
  Register leftYreg (
    .D(left_bat_temp), .Q({leftYout, left_bat_out}), .clk(controlled_buffer_1_out), .clr(reset));  // open: en
  Clock #(.highDuration(4), .lowDuration(4)) clock_4 (.out(clock_4_out));
  Multiplexer #(.width(8)) multiplexer_3 (
    .in0({ballY, y_ball}), .in1(8'h87), .out(multiplexer_3_out), .sel(init));  // open: en
  Multiplexer #(.width(8)) multiplexer_4 (
    .in0(vy_t), .in1({8{1'b1}}), .out(multiplexer_4_out), .sel(init));  // open: en
  Register yreg (.D(multiplexer_3_out), .Q(ball_y), .clk(clock_2_out));  // open: en, clr
  Register u_vy (.D(multiplexer_4_out), .Q(vy), .clk(clock_3_out));  // open: en, clr
  Counter counter_2 (
    .load(undriven), .count(hitTheLeftBall), .Q(scoreB), .clk(clock_3_out), .clr(reset));  // open: D, carry
  Register rightYreg (.D(in_4), .Q(rightBat), .clk(clock_4_out), .clr(reset));  // open: en
  ball_move ball_move_1 (
    .crash_x(x), .crash_y(y), .vx(vx), .vy(vy), .ball_x(ball_x), .ball_y(ball_y), .ball_x_2({ballX, x_ball}),
    .ball_y_2({ballY, y_ball}), .new_vx(vx_t), .new_vy(vy_t));
  Counter #(.width(1), .max('h1)) counter_3 (
    .count(init), .Q(counter_3_q), .clk(clock_4_out), .clr(reset));  // open: load, D, carry
  Comparator #(.width(1), .mode("unsigned")) comparator_2 (.a(1'b0), .b(counter_3_q), .eq(init));  // open: gt, lt

  assign out_5 = {5{1'b0}};
  assign rightYout = rightBat[7:3];

  // Other names for the same wires on the sheet: cdm8_score[7:0] = scoreB; left_bat[4:0] = leftYin;
  //   left_bat_out[7:3] = leftYout; player_score[7:0] = scoreA; right_bat[7:0] = in_4; right_bat_out[7:0] = rightBat;
  //   vx_temp[7:0] = vx; vy_temp[7:0] = vy; x_ball[7:3] = ballX; xball[7:0] = ball_x; y_ball[7:3] = ballY;
  //   yball[7:0] = ball_y
endmodule

// conv
module _5_to_32 (
  input  [4:0] in_1,
  output [31:0] out_2
);

  Shifter #(.width(32)) shifter_1 (.in(32'h1), .\dist (in_1), .out(out_2));
endmodule

module bat (
  input  [4:0] in_1,
  output [31:0] out_2
);

  wire [31:0] adder_1_out, adder_2_out, n5_to_32_1_out_2, shifter_1_out, shifter_2_out, shifter_3_out;

  _5_to_32 u_5_to_32_1 (.in_1(in_1), .out_2(n5_to_32_1_out_2));
  Shifter #(.width(32)) shifter_1 (.in(n5_to_32_1_out_2), .\dist (5'b00001), .out(shifter_1_out));
  Shifter #(.width(32)) shifter_2 (.in(shifter_1_out), .\dist (5'b00001), .out(shifter_2_out));
  Adder #(.width(32)) adder_1 (.a(shifter_1_out), .b(n5_to_32_1_out_2), .out(adder_1_out));  // open: cin, cout
  Shifter #(.width(32)) shifter_3 (.in(shifter_2_out), .\dist (5'b00001), .out(shifter_3_out));
  Adder #(.width(32)) adder_2 (.a(shifter_2_out), .b(adder_1_out), .out(adder_2_out));  // open: cin, cout
  Adder #(.width(32)) adder_3 (.a(shifter_3_out), .b(adder_2_out), .out(out_2));  // open: cin, cout
endmodule

module bat_move (
  input  [7:0] in_1,
  input  in_2,
  input  in_3,
  output [7:0] bat_y
);

  wire adder_1_cout, adder_2_cout, adder_3_cout, adder_4_cout, comparator_1_gt, controlled_buffer_1_out,
       controlled_buffer_2_out, not_1_out, or_1_out;
  wire [7:0] adder_1_out, adder_3_out, adder_4_out, multiplexer_1_out, multiplexer_2_out, undriven, y;

  // Probe on adder_1_out
  Adder adder_1 (.a(in_1), .b(8'h21), .out(adder_1_out), .cout(adder_1_cout));  // open: cin
  or or_1 (or_1_out, adder_1_cout, adder_3_cout);
  not not_1 (not_1_out, or_1_out);
  assign controlled_buffer_1_out = not_1_out ? in_2 : 1'bz;  // Controlled_Buffer controlled_buffer_1
  assign controlled_buffer_2_out = adder_4_cout ? in_3 : 1'bz;  // Controlled_Buffer controlled_buffer_2
  Adder adder_2 (.a(undriven), .b(y), .cout(adder_2_cout));  // open: out, cin
  // AND_Gate and_1 has open pins: in0=adder_2_cout, in1=comparator_1_gt, out=open
  Multiplexer #(.width(8)) multiplexer_1 (
    .in0(in_1), .in1(adder_3_out), .out(multiplexer_1_out), .sel(controlled_buffer_1_out));  // open: en
  Adder adder_3 (.a(in_1), .b(8'h7), .out(adder_3_out), .cout(adder_3_cout));  // open: cin
  Pull_Resistor pull_resistor_1 (.node(controlled_buffer_1_out));
  Multiplexer #(.width(8)) multiplexer_2 (
    .in0(in_1), .in1(adder_4_out), .out(multiplexer_2_out), .sel(controlled_buffer_2_out));  // open: en
  Adder adder_4 (.a(in_1), .b(8'hf9), .out(adder_4_out), .cout(adder_4_cout));  // open: cin
  Pull_Resistor pull_resistor_2 (.node(controlled_buffer_2_out));
  Comparator comparator_1 (.a(undriven), .b({8{1'b0}}), .gt(comparator_1_gt));  // open: eq, lt
  Multiplexer #(.width(8)) multiplexer_3 (
    .in0(multiplexer_1_out), .in1(multiplexer_2_out), .out(bat_y), .sel(controlled_buffer_2_out));  // open: en
endmodule

module leds (
  input  [7:0] in_1,
  input  [7:0] in_2,
  output [31:0] out_3
);

  wire clock_1_out, comparator_1_eq, controlled_buffer_1_out;
  wire [7:0] or_1_out;

  Clock #(.highDuration(100), .lowDuration(100)) clock_1 (.out(clock_1_out));
  assign controlled_buffer_1_out = comparator_1_eq ? clock_1_out : 1'bz;  // Controlled_Buffer controlled_buffer_1
  assign or_1_out = in_1 | in_2;  // OR_Gate or_1, 8 bits wide
  Multiplexer #(.width(32)) multiplexer_1 (
    .in0(32'h55555555), .in1(32'haaaaaaaa), .out(out_3), .sel(controlled_buffer_1_out));  // open: en
  Comparator comparator_1 (.a(or_1_out), .b(8'h19), .eq(comparator_1_eq));  // open: gt, lt
endmodule

module ball_move (
  input  crash_x,
  input  crash_y,
  input  [7:0] vx,
  input  [7:0] vy,
  input  [7:0] ball_x,
  input  [7:0] ball_y,
  output [7:0] ball_x_2,
  output [7:0] ball_y_2,
  output [7:0] new_vx,
  output [7:0] new_vy
);

  wire [7:0] if_1_res, if_2_res, inc_8_bit_2_out_2, neg_vx, not_1_out, not_2_out;

  assign not_1_out = ~vx;  // NOT_Gate not_1, 8 bits wide
  assign not_2_out = ~vy;  // NOT_Gate not_2, 8 bits wide
  \if  if_1 (.A(vx), .sel(crash_x), .B(neg_vx), .res(if_1_res));
  inc_8_bit inc_8_bit_1 (.in_1(not_1_out), .out_2(neg_vx));
  \if  if_2 (.A(vy), .sel(crash_y), .B(inc_8_bit_2_out_2), .res(if_2_res));
  inc_8_bit inc_8_bit_2 (.in_1(not_2_out), .out_2(inc_8_bit_2_out_2));
  Adder adder_1 (.a(if_1_res), .b(ball_x), .out(ball_x_2));  // open: cin, cout
  Adder adder_2 (.a(if_2_res), .b(ball_y), .out(ball_y_2));  // open: cin, cout
  Multiplexer #(.width(8)) multiplexer_1 (.in0(vx), .in1(neg_vx), .out(new_vx), .sel(crash_x));  // open: en
  Multiplexer #(.width(8)) multiplexer_2 (.in0(vy), .in1(inc_8_bit_2_out_2), .out(new_vy), .sel(crash_y));  // open: en
endmodule

module \if  (
  input  [7:0] A,
  input  sel,
  input  [7:0] B,
  output [7:0] res
);

  wire [7:0] and_1_out, and_2_out;
  wire [7:7] not_1_out;

  not not_1 (not_1_out[7], sel);
  assign and_1_out = A & {8{not_1_out[7]}};  // AND_Gate and_1, 8 bits wide
  assign and_2_out = {8{sel}} & B;  // AND_Gate and_2, 8 bits wide
  assign res = and_1_out | and_2_out;  // OR_Gate or_1, 8 bits wide
endmodule

module check_hit (
  input  [7:0] left_bat,
  input  [7:0] right_bat,
  input  [7:0] vx,
  input  [7:0] ball_x,
  input  [7:0] vy,
  input  [7:0] ball_y,
  output x_hit,
  output hitTheRightWall,
  output hitTheLeftWall,
  output y_hit
);

  wire adder_1_cout, adder_2_cout, adder_3_cout, adder_4_cout, and_2_out, and_3_out, and_4_out, and_5_out,
       and_6_out, check_carry_2_out_3, comparator_1_lt, comparator_2_lt, comparator_3_gt, comparator_4_gt,
       comparator_5_lt, comparator_6_eq, comparator_6_gt, comparator_7_eq, comparator_8_lt, comparator_9_eq,
       comparator_9_gt, comparator_10_eq, or_1_out, or_3_out, or_4_out;
  wire [7:0] adder_5_out, adder_6_out;

  Adder adder_1 (.a(ball_x), .b(vx), .cout(adder_1_cout));  // open: out, cin
  Comparator comparator_1 (.a(vx), .b({8{1'b0}}), .lt(comparator_1_lt));  // open: gt, eq
  Adder adder_2 (.a(ball_y), .b(vy), .cout(adder_2_cout));  // open: out, cin
  Comparator comparator_2 (.a(vy), .b({8{1'b0}}), .lt(comparator_2_lt));  // open: gt, eq
  Adder adder_3 (.a(vx), .b(ball_x), .cout(adder_3_cout));  // open: out, cin
  and and_1 (hitTheRightWall, adder_3_cout, comparator_3_gt);
  check_carry check_carry_1 (.in_1(comparator_1_lt), .in_2(adder_1_cout), .out_3(hitTheLeftWall));
  Adder adder_4 (.a(vy), .b(ball_y), .cout(adder_4_cout));  // open: out, cin
  and and_2 (and_2_out, adder_4_cout, comparator_4_gt);
  check_carry check_carry_2 (.in_1(comparator_2_lt), .in_2(adder_2_cout), .out_3(check_carry_2_out_3));
  Adder adder_5 (.a(8'h21), .b(left_bat), .out(adder_5_out));  // open: cin, cout
  Adder adder_6 (.a(8'h21), .b(right_bat), .out(adder_6_out));  // open: cin, cout
  Comparator comparator_3 (.a(vx), .b({8{1'b0}}), .gt(comparator_3_gt));  // open: eq, lt
  or or_1 (or_1_out, hitTheRightWall, hitTheLeftWall);
  Comparator comparator_4 (.a(vy), .b({8{1'b0}}), .gt(comparator_4_gt));  // open: eq, lt
  or or_2 (y_hit, and_2_out, check_carry_2_out_3);
  Comparator #(.mode("unsigned")) comparator_5 (.a(ball_y), .b(adder_5_out), .lt(comparator_5_lt));  // open: gt, eq
  Comparator #(.mode("unsigned")) comparator_6 (
    .a(ball_y), .b(left_bat), .gt(comparator_6_gt), .eq(comparator_6_eq));  // open: lt
  Comparator #(.width(5), .mode("unsigned")) comparator_7 (
    .a(5'b00001), .b(ball_x[7:3]), .eq(comparator_7_eq));  // open: gt, lt
  or or_3 (or_3_out, comparator_6_gt, comparator_6_eq);
  Comparator #(.mode("unsigned")) comparator_8 (.a(ball_y), .b(adder_6_out), .lt(comparator_8_lt));  // open: gt, eq
  Comparator #(.mode("unsigned")) comparator_9 (
    .a(ball_y), .b(right_bat), .gt(comparator_9_gt), .eq(comparator_9_eq));  // open: lt
  or or_4 (or_4_out, comparator_9_gt, comparator_9_eq);
  Comparator #(.width(5), .mode("unsigned")) comparator_10 (
    .a(5'b11101), .b(ball_x[7:3]), .eq(comparator_10_eq));  // open: gt, lt
  and and_3 (and_3_out, comparator_5_lt, or_3_out);
  and and_4 (and_4_out, comparator_8_lt, or_4_out);
  and and_5 (and_5_out, and_3_out, comparator_7_eq);
  and and_6 (and_6_out, and_4_out, comparator_10_eq);
  or or_5 (x_hit, and_5_out, and_6_out, or_1_out);

  // Other names for the same wires on the sheet: x[7:0] = ball_x; y[7:0] = ball_y
endmodule

module inc_8_bit (
  input  [7:0] in_1,
  output [7:0] out_2
);

  wire [7:1] and_1_out;
  wire [7:7] and_1_out_2;

  assign {and_1_out_2[7], and_1_out} = {and_1_out, 1'b1} & in_1;  // AND_Gate and_1, 8 bits wide
  assign out_2 = in_1 ^ {and_1_out, 1'b1};  // XOR_Gate xor_1, 8 bits wide
  // also tied to GND on the sheet: and_1_out_2[7]
endmodule

module check_carry (
  input  in_1,
  input  in_2,
  output out_3
);

  wire transistor_1_out;

  Transistor #(.\type ("n")) transistor_1 (.in(1'b1), .out(transistor_1_out), .gate(in_1));
  Transistor #(.gate("br")) transistor_2 (.in(transistor_1_out), .out(out_3), .gate(in_2));
  Pull_Resistor pull_resistor_1 (.node(out_3));
endmodule
